# Fritzing sketch OledArduino (saved by Fritzing 1.0.2b)
breadboards: 1

parts:
  OLED1 = OLED 128x64 I2C Monochrome Display VDD-GND
  Bauteil1 = Arduino Uno (Rev3)

nets:
  VDD: OLED1.VDD, Bauteil1.5V
  GND: OLED1.GND, Bauteil1.GND
  N1: OLED1.SCK, Bauteil1.A5/SCL
  N2: OLED1.SDA, Bauteil1.A4/SDA

custom parts:
  OLED 128x64 I2C Monochrome Display VDD-GND: OLED 128x64 I2C Monochrome Display. Note: there are two variants of this part, this one is the VDD GND SCK SDA variant. The other is GND VDD SCK SDA. Make sure you select the part that matches your module as using the incorrect part will probably destroy your module! In addition the mounting holes are marked on silkscreen but not by default drilled. If you want drilled mounting holes, copy a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
