# Fritzing sketch AdjustableRunningLight (saved by Fritzing 0.9.2b)
breadboards: 1

parts:
  Bauteil1 = Arduino Uno (Rev3)
  LED1 = LED - 5mm [color="Red (633nm)" package="5 mm [THT]"]
  LED2 = LED - 5mm [color="Red (633nm)" package="5 mm [THT]"]
  LED3 = LED - 5mm [color="Red (633nm)" package="5 mm [THT]"]
  LED4 = LED - 5mm [color="Red (633nm)" package="5 mm [THT]"]
  LED5 = LED - 5mm [color="Red (633nm)" package="5 mm [THT]"]
  LED6 = LED - 5mm [color="Red (633nm)" package="5 mm [THT]"]
  LED7 = LED - 5mm [color="Red (633nm)" package="5 mm [THT]"]
  LED8 = LED - 5mm [color="Red (633nm)" package="5 mm [THT]"]
  R1 = Resistor [tolerance=±5% resistance=220 package="0402 [SMD]"]
  R2 = Resistor [tolerance=±5% resistance=220 package="0402 [SMD]"]
  R3 = Resistor [tolerance=±5% resistance=220 package="0402 [SMD]"]
  R4 = Resistor [tolerance=±5% resistance=220 package="0402 [SMD]"]
  R5 = Resistor [tolerance=±5% resistance=220 package="0402 [SMD]"]
  R6 = Resistor [tolerance=±5% resistance=220 package="0402 [SMD]"]
  R7 = Resistor [tolerance=±5% resistance=220 package="0402 [SMD]"]
  R8 = Resistor [tolerance=±5% resistance=220 package="0402 [SMD]"]
  U1 = POT [package=pot_alpha_rv16af-20]

nets:
  N1: Bauteil1.A0, U1.S
  N2: Bauteil1.D10_PWM/SS, R4.Pin_0
  N3: Bauteil1.D11_PWM/MOSI, R3.Pin_0
  N4: Bauteil1.D12/MISO, R2.Pin_0
  N5: Bauteil1.D13/SCK, R1.Pin_0
  N6: Bauteil1.GND, LED1.cathode, LED2.cathode, LED3.cathode, LED4.cathode, LED5.cathode, LED6.cathode, LED7.cathode, LED8.cathode, U1.E
  N7: Bauteil1.D3_PWM, R8.Pin_0
  N8: Bauteil1.D4, R7.Pin_0
  N9: Bauteil1.D5_PWM, R6.Pin_0
  N10: Bauteil1.D6_PWM, R5.Pin_0
  N11: Bauteil1.5V, U1.A
  N12: LED1.anode, R2.Pin_1
  N13: LED2.anode, R3.Pin_1
  N14: LED3.anode, R4.Pin_1
  N15: LED4.anode, R5.Pin_1
  N16: LED5.anode, R6.Pin_1
  N17: LED6.anode, R7.Pin_1
  N18: LED7.anode, R8.Pin_1
  N19: LED8.anode, R1.Pin_1
